// Logisim project CPU.circ as structural Verilog
module halfAdder (
  input  rs1,
  input  rs2,
  input  CarryIn,
  output rd,
  output CarryOut
);

  wire and_1_out, and_2_out, or_1_out;

  xor xor_1 (rd, rs1, rs2, CarryIn);
  and and_1 (and_1_out, rs1, rs2);
  or or_1 (or_1_out, rs1, rs2);
  and and_2 (and_2_out, or_1_out, CarryIn);
  or or_2 (CarryOut, and_1_out, and_2_out);
endmodule

module fullAdder8 (
  input  [7:0] rs1,
  input  [7:0] rs2,
  input  CarryIn,
  output [7:0] rd,
  output CarryOut
);

  wire halfadder_1_carryout, halfadder_2_carryout, halfadder_3_carryout, halfadder_4_carryout,
       halfadder_5_carryout, halfadder_6_carryout, halfadder_7_carryout;

  halfAdder halfadder_1 (.rs1(rs1[0]), .rs2(rs2[0]), .CarryIn(CarryIn), .rd(rd[0]), .CarryOut(halfadder_1_carryout));
  halfAdder halfadder_2 (
    .rs1(rs1[1]), .rs2(rs2[1]), .CarryIn(halfadder_1_carryout), .rd(rd[1]), .CarryOut(halfadder_2_carryout));
  halfAdder halfadder_3 (
    .rs1(rs1[2]), .rs2(rs2[2]), .CarryIn(halfadder_2_carryout), .rd(rd[2]), .CarryOut(halfadder_3_carryout));
  halfAdder halfadder_4 (
    .rs1(rs1[3]), .rs2(rs2[3]), .CarryIn(halfadder_3_carryout), .rd(rd[3]), .CarryOut(halfadder_4_carryout));
  halfAdder halfadder_5 (
    .rs1(rs1[4]), .rs2(rs2[4]), .CarryIn(halfadder_4_carryout), .rd(rd[4]), .CarryOut(halfadder_5_carryout));
  halfAdder halfadder_6 (
    .rs1(rs1[5]), .rs2(rs2[5]), .CarryIn(halfadder_5_carryout), .rd(rd[5]), .CarryOut(halfadder_6_carryout));
  halfAdder halfadder_7 (
    .rs1(rs1[6]), .rs2(rs2[6]), .CarryIn(halfadder_6_carryout), .rd(rd[6]), .CarryOut(halfadder_7_carryout));
  halfAdder halfadder_8 (.rs1(rs1[7]), .rs2(rs2[7]), .CarryIn(halfadder_7_carryout), .rd(rd[7]), .CarryOut(CarryOut));
endmodule

module integerAdder8 (
  input  [7:0] rs1,
  input  [7:0] rs2,
  input  CarryIn,
  output [7:0] rd,
  output CarryOut
);

  fullAdder8 fulladder8_1 (.rs1(rs1), .rs2(rs2), .CarryIn(CarryIn), .rd(rd), .CarryOut(CarryOut));

  // Notes on the sheet:
  //   Signed vs unsigned does not matter for integer addition/substraction
endmodule

module integerMultiply8 (
  input  [7:0] rs1,
  input  [7:0] rs2,
  output [7:0] lowerProduct,
  output [7:0] upperProduct
);

  wire fulladder16_1_carryout, fulladder16_2_carryout, fulladder16_3_carryout, fulladder16_4_carryout,
       fulladder16_5_carryout, fulladder16_6_carryout;
  wire [7:0] and8_1_rd, and8_2_rd, and8_3_rd, and8_4_rd, and8_5_rd, and8_6_rd, and8_7_rd, and8_8_rd,
       fulladder16_1_lowersum, fulladder16_1_uppersum, fulladder16_2_lowersum, fulladder16_2_uppersum,
       fulladder16_3_lowersum, fulladder16_3_uppersum, fulladder16_4_lowersum, fulladder16_4_uppersum,
       fulladder16_5_lowersum, fulladder16_5_uppersum, fulladder16_6_lowersum, fulladder16_6_uppersum,
       lshft16_trunc_1_lowerout, lshft16_trunc_1_upperout, lshft16_trunc_2_lowerout,
       lshft16_trunc_2_upperout, lshft16_trunc_3_lowerout, lshft16_trunc_3_upperout,
       lshft16_trunc_4_lowerout, lshft16_trunc_4_upperout, lshft16_trunc_5_lowerout,
       lshft16_trunc_5_upperout, lshft16_trunc_6_lowerout, lshft16_trunc_6_upperout,
       lshft16_trunc_7_lowerout, lshft16_trunc_7_upperout, lshft16_trunc_8_lowerout,
       lshft16_trunc_8_upperout, lshft16_trunc_9_lowerout, lshft16_trunc_9_upperout,
       lshft16_trunc_10_lowerout, lshft16_trunc_10_upperout, lshft16_trunc_11_lowerout,
       lshft16_trunc_11_upperout, lshft16_trunc_12_lowerout, lshft16_trunc_12_upperout,
       lshft16_trunc_13_lowerout, lshft16_trunc_13_upperout, lshft16_trunc_14_lowerout,
       lshft16_trunc_14_upperout, lshft16_trunc_15_lowerout, lshft16_trunc_15_upperout,
       lshft16_trunc_16_lowerout, lshft16_trunc_16_upperout, lshft16_trunc_17_lowerout,
       lshft16_trunc_17_upperout, lshft16_trunc_18_lowerout, lshft16_trunc_18_upperout,
       lshft16_trunc_19_lowerout, lshft16_trunc_19_upperout, lshft16_trunc_20_lowerout,
       lshft16_trunc_20_upperout, lshft16_trunc_21_lowerout, lshft16_trunc_21_upperout,
       lshft16_trunc_22_lowerout, lshft16_trunc_22_upperout, lshft16_trunc_23_lowerout,
       lshft16_trunc_23_upperout, lshft16_trunc_24_lowerout, lshft16_trunc_24_upperout,
       lshft16_trunc_25_lowerout, lshft16_trunc_25_upperout, lshft16_trunc_26_lowerout,
       lshft16_trunc_26_upperout, lshft16_trunc_27_lowerout, lshft16_trunc_27_upperout,
       lshft16_trunc_28_lowerout, lshft16_trunc_28_upperout, not_1_out;

  not not_1 (not_1_out[0], 1'b1);
  not not_2 (not_1_out[1], 1'b1);
  not not_3 (not_1_out[2], 1'b1);
  not not_4 (not_1_out[3], 1'b1);
  not not_5 (not_1_out[4], 1'b1);
  not not_6 (not_1_out[5], 1'b1);
  not not_7 (not_1_out[6], 1'b1);
  not not_8 (not_1_out[7], 1'b1);
  and8 and8_1 (.rs1(rs1), .rs2({8{rs2[0]}}), .rd(and8_1_rd));
  and8 and8_2 (.rs1(rs1), .rs2({8{rs2[1]}}), .rd(and8_2_rd));
  and8 and8_3 (.rs1(rs1), .rs2({8{rs2[2]}}), .rd(and8_3_rd));
  and8 and8_4 (.rs1(rs1), .rs2({8{rs2[3]}}), .rd(and8_4_rd));
  and8 and8_5 (.rs1(rs1), .rs2({8{rs2[4]}}), .rd(and8_5_rd));
  and8 and8_6 (.rs1(rs1), .rs2({8{rs2[5]}}), .rd(and8_6_rd));
  and8 and8_7 (.rs1(rs1), .rs2({8{rs2[6]}}), .rd(and8_7_rd));
  and8 and8_8 (.rs1(rs1), .rs2({8{rs2[7]}}), .rd(and8_8_rd));
  lshft16_trunc lshft16_trunc_1 (
    .lowerA(and8_2_rd), .upperA(not_1_out), .lowerOut(lshft16_trunc_1_lowerout),
    .upperOut(lshft16_trunc_1_upperout));
  lshft16_trunc lshft16_trunc_2 (
    .lowerA(and8_3_rd), .upperA(not_1_out), .lowerOut(lshft16_trunc_2_lowerout),
    .upperOut(lshft16_trunc_2_upperout));
  lshft16_trunc lshft16_trunc_3 (
    .lowerA(and8_4_rd), .upperA(not_1_out), .lowerOut(lshft16_trunc_3_lowerout),
    .upperOut(lshft16_trunc_3_upperout));
  lshft16_trunc lshft16_trunc_4 (
    .lowerA(and8_5_rd), .upperA(not_1_out), .lowerOut(lshft16_trunc_4_lowerout),
    .upperOut(lshft16_trunc_4_upperout));
  lshft16_trunc lshft16_trunc_5 (
    .lowerA(and8_6_rd), .upperA(not_1_out), .lowerOut(lshft16_trunc_5_lowerout),
    .upperOut(lshft16_trunc_5_upperout));
  lshft16_trunc lshft16_trunc_6 (
    .lowerA(and8_7_rd), .upperA(not_1_out), .lowerOut(lshft16_trunc_6_lowerout),
    .upperOut(lshft16_trunc_6_upperout));
  lshft16_trunc lshft16_trunc_7 (
    .lowerA(and8_8_rd), .upperA(not_1_out), .lowerOut(lshft16_trunc_7_lowerout),
    .upperOut(lshft16_trunc_7_upperout));
  lshft16_trunc lshft16_trunc_8 (
    .lowerA(lshft16_trunc_2_lowerout), .upperA(lshft16_trunc_2_upperout),
    .lowerOut(lshft16_trunc_8_lowerout), .upperOut(lshft16_trunc_8_upperout));
  lshft16_trunc lshft16_trunc_9 (
    .lowerA(lshft16_trunc_3_lowerout), .upperA(lshft16_trunc_3_upperout),
    .lowerOut(lshft16_trunc_9_lowerout), .upperOut(lshft16_trunc_9_upperout));
  lshft16_trunc lshft16_trunc_10 (
    .lowerA(lshft16_trunc_4_lowerout), .upperA(lshft16_trunc_4_upperout),
    .lowerOut(lshft16_trunc_10_lowerout), .upperOut(lshft16_trunc_10_upperout));
  lshft16_trunc lshft16_trunc_11 (
    .lowerA(lshft16_trunc_5_lowerout), .upperA(lshft16_trunc_5_upperout),
    .lowerOut(lshft16_trunc_11_lowerout), .upperOut(lshft16_trunc_11_upperout));
  lshft16_trunc lshft16_trunc_12 (
    .lowerA(lshft16_trunc_6_lowerout), .upperA(lshft16_trunc_6_upperout),
    .lowerOut(lshft16_trunc_12_lowerout), .upperOut(lshft16_trunc_12_upperout));
  lshft16_trunc lshft16_trunc_13 (
    .lowerA(lshft16_trunc_7_lowerout), .upperA(lshft16_trunc_7_upperout),
    .lowerOut(lshft16_trunc_13_lowerout), .upperOut(lshft16_trunc_13_upperout));
  lshft16_trunc lshft16_trunc_14 (
    .lowerA(lshft16_trunc_9_lowerout), .upperA(lshft16_trunc_9_upperout),
    .lowerOut(lshft16_trunc_14_lowerout), .upperOut(lshft16_trunc_14_upperout));
  lshft16_trunc lshft16_trunc_15 (
    .lowerA(lshft16_trunc_10_lowerout), .upperA(lshft16_trunc_10_upperout),
    .lowerOut(lshft16_trunc_15_lowerout), .upperOut(lshft16_trunc_15_upperout));
  lshft16_trunc lshft16_trunc_16 (
    .lowerA(lshft16_trunc_11_lowerout), .upperA(lshft16_trunc_11_upperout),
    .lowerOut(lshft16_trunc_16_lowerout), .upperOut(lshft16_trunc_16_upperout));
  lshft16_trunc lshft16_trunc_17 (
    .lowerA(lshft16_trunc_12_lowerout), .upperA(lshft16_trunc_12_upperout),
    .lowerOut(lshft16_trunc_17_lowerout), .upperOut(lshft16_trunc_17_upperout));
  lshft16_trunc lshft16_trunc_18 (
    .lowerA(lshft16_trunc_13_lowerout), .upperA(lshft16_trunc_13_upperout),
    .lowerOut(lshft16_trunc_18_lowerout), .upperOut(lshft16_trunc_18_upperout));
  lshft16_trunc lshft16_trunc_19 (
    .lowerA(lshft16_trunc_15_lowerout), .upperA(lshft16_trunc_15_upperout),
    .lowerOut(lshft16_trunc_19_lowerout), .upperOut(lshft16_trunc_19_upperout));
  lshft16_trunc lshft16_trunc_20 (
    .lowerA(lshft16_trunc_16_lowerout), .upperA(lshft16_trunc_16_upperout),
    .lowerOut(lshft16_trunc_20_lowerout), .upperOut(lshft16_trunc_20_upperout));
  lshft16_trunc lshft16_trunc_21 (
    .lowerA(lshft16_trunc_17_lowerout), .upperA(lshft16_trunc_17_upperout),
    .lowerOut(lshft16_trunc_21_lowerout), .upperOut(lshft16_trunc_21_upperout));
  lshft16_trunc lshft16_trunc_22 (
    .lowerA(lshft16_trunc_18_lowerout), .upperA(lshft16_trunc_18_upperout),
    .lowerOut(lshft16_trunc_22_lowerout), .upperOut(lshft16_trunc_22_upperout));
  lshft16_trunc lshft16_trunc_23 (
    .lowerA(lshft16_trunc_20_lowerout), .upperA(lshft16_trunc_20_upperout),
    .lowerOut(lshft16_trunc_23_lowerout), .upperOut(lshft16_trunc_23_upperout));
  lshft16_trunc lshft16_trunc_24 (
    .lowerA(lshft16_trunc_21_lowerout), .upperA(lshft16_trunc_21_upperout),
    .lowerOut(lshft16_trunc_24_lowerout), .upperOut(lshft16_trunc_24_upperout));
  lshft16_trunc lshft16_trunc_25 (
    .lowerA(lshft16_trunc_22_lowerout), .upperA(lshft16_trunc_22_upperout),
    .lowerOut(lshft16_trunc_25_lowerout), .upperOut(lshft16_trunc_25_upperout));
  lshft16_trunc lshft16_trunc_26 (
    .lowerA(lshft16_trunc_24_lowerout), .upperA(lshft16_trunc_24_upperout),
    .lowerOut(lshft16_trunc_26_lowerout), .upperOut(lshft16_trunc_26_upperout));
  lshft16_trunc lshft16_trunc_27 (
    .lowerA(lshft16_trunc_25_lowerout), .upperA(lshft16_trunc_25_upperout),
    .lowerOut(lshft16_trunc_27_lowerout), .upperOut(lshft16_trunc_27_upperout));
  lshft16_trunc lshft16_trunc_28 (
    .lowerA(lshft16_trunc_27_lowerout), .upperA(lshft16_trunc_27_upperout),
    .lowerOut(lshft16_trunc_28_lowerout), .upperOut(lshft16_trunc_28_upperout));
  fullAdder16 fulladder16_1 (
    .lowerA(and8_1_rd), .upperA(not_1_out), .lowerB(lshft16_trunc_1_lowerout),
    .UpperB(lshft16_trunc_1_upperout), .lowerSum(fulladder16_1_lowersum), .upperSum(fulladder16_1_uppersum),
    .CarryOut(fulladder16_1_carryout));  // open: CarryIn
  fullAdder16 fulladder16_2 (
    .lowerA(fulladder16_1_lowersum), .upperA(fulladder16_1_uppersum), .lowerB(lshft16_trunc_8_lowerout),
    .UpperB(lshft16_trunc_8_upperout), .CarryIn(fulladder16_1_carryout), .lowerSum(fulladder16_2_lowersum),
    .upperSum(fulladder16_2_uppersum), .CarryOut(fulladder16_2_carryout));
  fullAdder16 fulladder16_3 (
    .lowerA(fulladder16_2_lowersum), .upperA(fulladder16_2_uppersum), .lowerB(lshft16_trunc_14_lowerout),
    .UpperB(lshft16_trunc_14_upperout), .CarryIn(fulladder16_2_carryout), .lowerSum(fulladder16_3_lowersum),
    .upperSum(fulladder16_3_uppersum), .CarryOut(fulladder16_3_carryout));
  fullAdder16 fulladder16_4 (
    .lowerA(fulladder16_3_lowersum), .upperA(fulladder16_3_uppersum), .lowerB(lshft16_trunc_19_lowerout),
    .UpperB(lshft16_trunc_19_upperout), .CarryIn(fulladder16_3_carryout), .lowerSum(fulladder16_4_lowersum),
    .upperSum(fulladder16_4_uppersum), .CarryOut(fulladder16_4_carryout));
  fullAdder16 fulladder16_5 (
    .lowerA(fulladder16_4_lowersum), .upperA(fulladder16_4_uppersum), .lowerB(lshft16_trunc_23_lowerout),
    .UpperB(lshft16_trunc_23_upperout), .CarryIn(fulladder16_4_carryout), .lowerSum(fulladder16_5_lowersum),
    .upperSum(fulladder16_5_uppersum), .CarryOut(fulladder16_5_carryout));
  fullAdder16 fulladder16_6 (
    .lowerA(fulladder16_5_lowersum), .upperA(fulladder16_5_uppersum), .lowerB(lshft16_trunc_26_lowerout),
    .UpperB(lshft16_trunc_26_upperout), .CarryIn(fulladder16_5_carryout), .lowerSum(fulladder16_6_lowersum),
    .upperSum(fulladder16_6_uppersum), .CarryOut(fulladder16_6_carryout));
  fullAdder16 fulladder16_7 (
    .lowerA(fulladder16_6_lowersum), .upperA(fulladder16_6_uppersum), .lowerB(lshft16_trunc_28_lowerout),
    .UpperB(lshft16_trunc_28_upperout), .CarryIn(fulladder16_6_carryout), .lowerSum(lowerProduct),
    .upperSum(upperProduct));  // open: CarryOut
endmodule

module xor8 (
  input  [7:0] rs1,
  input  [7:0] rs2,
  output [7:0] rd
);

  xor xor_1 (rd[0], rs1[0], rs2[0]);
  xor xor_2 (rd[1], rs1[1], rs2[1]);
  xor xor_3 (rd[2], rs1[2], rs2[2]);
  xor xor_4 (rd[3], rs1[3], rs2[3]);
  xor xor_5 (rd[4], rs1[4], rs2[4]);
  xor xor_6 (rd[5], rs1[5], rs2[5]);
  xor xor_7 (rd[6], rs1[6], rs2[6]);
  xor xor_8 (rd[7], rs1[7], rs2[7]);
endmodule

module and8 (
  input  [7:0] rs1,
  input  [7:0] rs2,
  output [7:0] rd
);

  and and_1 (rd[0], rs1[0], rs2[0]);
  and and_2 (rd[1], rs1[1], rs2[1]);
  and and_3 (rd[2], rs1[2], rs2[2]);
  and and_4 (rd[3], rs1[3], rs2[3]);
  and and_5 (rd[4], rs1[4], rs2[4]);
  and and_6 (rd[5], rs1[5], rs2[5]);
  and and_7 (rd[6], rs1[6], rs2[6]);
  and and_8 (rd[7], rs1[7], rs2[7]);
endmodule

module or8 (
  input  [7:0] rs1,
  input  [7:0] rs2,
  output [7:0] rd
);

  or or_1 (rd[0], rs1[0], rs2[0]);
  or or_2 (rd[1], rs1[1], rs2[1]);
  or or_3 (rd[2], rs1[2], rs2[2]);
  or or_4 (rd[3], rs1[3], rs2[3]);
  or or_5 (rd[4], rs1[4], rs2[4]);
  or or_6 (rd[5], rs1[5], rs2[5]);
  or or_7 (rd[6], rs1[6], rs2[6]);
  or or_8 (rd[7], rs1[7], rs2[7]);
endmodule

module buf8 (
  input  [7:0] rs1,
  output [7:0] rd
);


  assign rd = rs1;
endmodule

module integerDivide8 (
  input  [7:0] rs1,
  input  [7:0] rs2,
  output [7:0] Q,
  output [7:0] R
);


  // Notes on the sheet:
  //   Computes A / B to have quotient Q and remainder R
endmodule

module lshft8 (
  input  [7:0] rs1,
  output [7:0] rd
);


  assign rd = {rs1[6:0], rs1[7]};
endmodule

module rshft8 (
  input  [7:0] rs1,
  output [7:0] rd
);


  assign rd = {rs1[0], rs1[7:1]};
endmodule

module lshft8_trunc (
  input  [7:0] rs1,
  output [7:0] rd
);

  not not_1 (rd[0], 1'b1);

  assign rd[7:1] = rs1[6:0];
endmodule

module rshft8_trunc (
  input  [7:0] rs1,
  output [7:0] rd
);

  not not_1 (rd[7], 1'b1);

  assign rd[6:0] = rs1[7:1];
endmodule

module fullAdder16 (
  input  [7:0] lowerA,
  input  [7:0] upperA,
  input  [7:0] lowerB,
  input  [7:0] UpperB,
  input  CarryIn,
  output [7:0] lowerSum,
  output [7:0] upperSum,
  output CarryOut
);

  wire halfadder_1_carryout, halfadder_2_carryout, halfadder_3_carryout, halfadder_4_carryout,
       halfadder_5_carryout, halfadder_6_carryout, halfadder_7_carryout, halfadder_8_carryout,
       halfadder_9_carryout, halfadder_10_carryout, halfadder_11_carryout, halfadder_12_carryout,
       halfadder_13_carryout, halfadder_14_carryout, halfadder_15_carryout;

  halfAdder halfadder_1 (
    .rs1(lowerA[0]), .rs2(lowerB[0]), .CarryIn(CarryIn), .rd(lowerSum[0]), .CarryOut(halfadder_1_carryout));
  halfAdder halfadder_2 (
    .rs1(lowerA[1]), .rs2(lowerB[1]), .CarryIn(halfadder_1_carryout), .rd(lowerSum[1]),
    .CarryOut(halfadder_2_carryout));
  halfAdder halfadder_3 (
    .rs1(lowerA[2]), .rs2(lowerB[2]), .CarryIn(halfadder_2_carryout), .rd(lowerSum[2]),
    .CarryOut(halfadder_3_carryout));
  halfAdder halfadder_4 (
    .rs1(lowerA[3]), .rs2(lowerB[3]), .CarryIn(halfadder_3_carryout), .rd(lowerSum[3]),
    .CarryOut(halfadder_4_carryout));
  halfAdder halfadder_5 (
    .rs1(lowerA[4]), .rs2(lowerB[4]), .CarryIn(halfadder_4_carryout), .rd(lowerSum[4]),
    .CarryOut(halfadder_5_carryout));
  halfAdder halfadder_6 (
    .rs1(lowerA[5]), .rs2(lowerB[5]), .CarryIn(halfadder_5_carryout), .rd(lowerSum[5]),
    .CarryOut(halfadder_6_carryout));
  halfAdder halfadder_7 (
    .rs1(lowerA[6]), .rs2(lowerB[6]), .CarryIn(halfadder_6_carryout), .rd(lowerSum[6]),
    .CarryOut(halfadder_7_carryout));
  halfAdder halfadder_8 (
    .rs1(lowerA[7]), .rs2(lowerB[7]), .CarryIn(halfadder_7_carryout), .rd(lowerSum[7]),
    .CarryOut(halfadder_8_carryout));
  halfAdder halfadder_9 (
    .rs1(upperA[0]), .rs2(UpperB[0]), .CarryIn(halfadder_8_carryout), .rd(upperSum[0]),
    .CarryOut(halfadder_9_carryout));
  halfAdder halfadder_10 (
    .rs1(upperA[1]), .rs2(UpperB[1]), .CarryIn(halfadder_9_carryout), .rd(upperSum[1]),
    .CarryOut(halfadder_10_carryout));
  halfAdder halfadder_11 (
    .rs1(upperA[2]), .rs2(UpperB[2]), .CarryIn(halfadder_10_carryout), .rd(upperSum[2]),
    .CarryOut(halfadder_11_carryout));
  halfAdder halfadder_12 (
    .rs1(upperA[3]), .rs2(UpperB[3]), .CarryIn(halfadder_11_carryout), .rd(upperSum[3]),
    .CarryOut(halfadder_12_carryout));
  halfAdder halfadder_13 (
    .rs1(upperA[4]), .rs2(UpperB[4]), .CarryIn(halfadder_12_carryout), .rd(upperSum[4]),
    .CarryOut(halfadder_13_carryout));
  halfAdder halfadder_14 (
    .rs1(upperA[5]), .rs2(UpperB[5]), .CarryIn(halfadder_13_carryout), .rd(upperSum[5]),
    .CarryOut(halfadder_14_carryout));
  halfAdder halfadder_15 (
    .rs1(upperA[6]), .rs2(UpperB[6]), .CarryIn(halfadder_14_carryout), .rd(upperSum[6]),
    .CarryOut(halfadder_15_carryout));
  halfAdder halfadder_16 (
    .rs1(upperA[7]), .rs2(UpperB[7]), .CarryIn(halfadder_15_carryout), .rd(upperSum[7]), .CarryOut(CarryOut));
endmodule

module lshft16_trunc (
  input  [7:0] lowerA,
  input  [7:0] upperA,
  output [7:0] lowerOut,
  output [7:0] upperOut
);

  not not_1 (lowerOut[0], 1'b1);

  assign lowerOut[7:1] = lowerA[6:0];
  assign upperOut = {upperA[6:0], lowerA[7]};
endmodule

module rshft16_trunc (
  input  [7:0] lowerA,
  input  [7:0] upperA,
  output [7:0] lowerOut,
  output [7:0] upperOut
);

  not not_1 (upperOut[7], 1'b1);

  assign lowerOut = {upperA[0], lowerA[7:1]};
  assign upperOut[6:0] = upperA[7:1];
endmodule

module slt8 (
  input  [7:0] A,
  input  [7:0] B
);

  wire [7:0] fulladder8_1_rd, fulladder8_2_rd;
  wire [7:7] not8_1_rd;

  not8 not8_1 (.rs1(A), .rd({8{not8_1_rd[7]}}));
  not8 not8_2 (.rs1(B), .rd({8{not8_1_rd[7]}}));
  fullAdder8 fulladder8_1 (
    .rs1({8{not8_1_rd[7]}}), .rs2({8{not8_1_rd[7]}}), .rd(fulladder8_1_rd));  // open: CarryIn, CarryOut
  fullAdder8 fulladder8_2 (
    .rs1({8{not8_1_rd[7]}}), .rs2({8{not8_1_rd[7]}}), .rd(fulladder8_2_rd));  // open: CarryIn, CarryOut
  fullAdder8 fulladder8_3 (.rs1(fulladder8_1_rd), .rs2(fulladder8_2_rd));  // open: CarryIn, rd, CarryOut
  // also tied to VCC on the sheet: not8_1_rd[7]

  // Notes on the sheet:
  //   Compliment INT(1) = 1111 1111
  //   Compliment INT(-1) = 0000 0001
  //   Two's Complement must be performed before operating and before returning
endmodule

module not8 (
  input  [7:0] rs1,
  output [7:0] rd
);

  not not_1 (rd[0], rs1[0]);
  not not_2 (rd[1], rs1[1]);
  not not_3 (rd[2], rs1[2]);
  not not_4 (rd[3], rs1[3]);
  not not_5 (rd[4], rs1[4]);
  not not_6 (rd[5], rs1[5]);
  not not_7 (rd[6], rs1[6]);
  not not_8 (rd[7], rs1[7]);
endmodule

module sltu8 (
  input  [7:0] rs1,
  input  [7:0] rs2,
  output out_3,
  output [7:0] rd
);

  wire [7:0] fulladder8_1_rd, fulladder8_2_rd, not8_1_rd;

  not not_1 (rd[7], 1'b1);
  not8 not8_1 (.rs1(rs2), .rd(not8_1_rd));
  fullAdder8 fulladder8_1 (.rs1(not8_1_rd), .rs2({{7{rd[7]}}, 1'b1}), .rd(fulladder8_1_rd));  // open: CarryIn, CarryOut
  fullAdder8 fulladder8_2 (.rs1(rs1), .rs2(fulladder8_1_rd), .rd(fulladder8_2_rd), .CarryOut(out_3));  // open: CarryIn
  and and_1 (rd[0], fulladder8_2_rd[7], 1'b1);

  assign rd[6:1] = {6{rd[7]}};

  // Notes on the sheet:
  //   rs1 < rs2 ? 1 : 0
  //   For unsigned: A - B = A + (~B + 1)
  //   Two's Complement must be performed before operating and before returning (UNSIGNED INPUTS)
  //   If rd[7] is set: A - B < 0
  //   If rd[7] is not: A - B >= 0
  //   8-bit output since eventually the instruction will require a destination register
endmodule
