// Logisim project CPU.circ as structural Verilog
module halfAdder (
  input  A,
  input  B,
  input  CarryIn,
  output Sum,
  output CarryOut
);

  wire and_1_out, and_2_out, or_1_out;

  xor xor_1 (Sum, A, B, CarryIn);
  and and_1 (and_1_out, A, B);
  or or_1 (or_1_out, A, B);
  and and_2 (and_2_out, or_1_out, CarryIn);
  or or_2 (CarryOut, and_1_out, and_2_out);
endmodule

module fullAdder8 (
  input  [7:0] A,
  input  [7:0] B,
  input  CarryIn,
  output [7:0] Sum,
  output CarryOut
);

  wire halfadder_1_carryout, halfadder_2_carryout, halfadder_3_carryout, halfadder_4_carryout,
       halfadder_5_carryout, halfadder_6_carryout, halfadder_7_carryout;

  halfAdder halfadder_1 (.A(A[0]), .B(B[0]), .CarryIn(CarryIn), .Sum(Sum[0]), .CarryOut(halfadder_1_carryout));
  halfAdder halfadder_2 (
    .A(A[1]), .B(B[1]), .CarryIn(halfadder_1_carryout), .Sum(Sum[1]), .CarryOut(halfadder_2_carryout));
  halfAdder halfadder_3 (
    .A(A[2]), .B(B[2]), .CarryIn(halfadder_2_carryout), .Sum(Sum[2]), .CarryOut(halfadder_3_carryout));
  halfAdder halfadder_4 (
    .A(A[3]), .B(B[3]), .CarryIn(halfadder_3_carryout), .Sum(Sum[3]), .CarryOut(halfadder_4_carryout));
  halfAdder halfadder_5 (
    .A(A[4]), .B(B[4]), .CarryIn(halfadder_4_carryout), .Sum(Sum[4]), .CarryOut(halfadder_5_carryout));
  halfAdder halfadder_6 (
    .A(A[5]), .B(B[5]), .CarryIn(halfadder_5_carryout), .Sum(Sum[5]), .CarryOut(halfadder_6_carryout));
  halfAdder halfadder_7 (
    .A(A[6]), .B(B[6]), .CarryIn(halfadder_6_carryout), .Sum(Sum[6]), .CarryOut(halfadder_7_carryout));
  halfAdder halfadder_8 (.A(A[7]), .B(B[7]), .CarryIn(halfadder_7_carryout), .Sum(Sum[7]), .CarryOut(CarryOut));
endmodule

module integerAdder8 (
  input  [7:0] A,
  input  [7:0] B,
  input  CarryIn,
  output [7:0] Sum,
  output CarryOut
);

  fullAdder8 fulladder8_1 (.A(A), .B(B), .CarryIn(CarryIn), .Sum(Sum), .CarryOut(CarryOut));
endmodule

module integerMultiply8 (
  input  [7:0] A,
  input  [7:0] B,
  output [7:0] lowerProduct,
  output [7:0] upperProduct
);

  wire fulladder16_1_carryout, fulladder16_2_carryout, fulladder16_3_carryout, fulladder16_4_carryout,
       fulladder16_5_carryout, fulladder16_6_carryout;
  wire [7:0] and8_1_o, and8_2_o, and8_3_o, and8_4_o, and8_5_o, and8_6_o, and8_7_o, and8_8_o,
       fulladder16_1_lowersum, fulladder16_1_uppersum, fulladder16_2_lowersum, fulladder16_2_uppersum,
       fulladder16_3_lowersum, fulladder16_3_uppersum, fulladder16_4_lowersum, fulladder16_4_uppersum,
       fulladder16_5_lowersum, fulladder16_5_uppersum, fulladder16_6_lowersum, fulladder16_6_uppersum,
       lshft16_trunc_1_lowerout, lshft16_trunc_1_upperout, lshft16_trunc_2_lowerout,
       lshft16_trunc_2_upperout, lshft16_trunc_3_lowerout, lshft16_trunc_3_upperout,
       lshft16_trunc_4_lowerout, lshft16_trunc_4_upperout, lshft16_trunc_5_lowerout,
       lshft16_trunc_5_upperout, lshft16_trunc_6_lowerout, lshft16_trunc_6_upperout,
       lshft16_trunc_7_lowerout, lshft16_trunc_7_upperout, lshft16_trunc_8_lowerout,
       lshft16_trunc_8_upperout, lshft16_trunc_9_lowerout, lshft16_trunc_9_upperout,
       lshft16_trunc_10_lowerout, lshft16_trunc_10_upperout, lshft16_trunc_11_lowerout,
       lshft16_trunc_11_upperout, lshft16_trunc_12_lowerout, lshft16_trunc_12_upperout,
       lshft16_trunc_13_lowerout, lshft16_trunc_13_upperout, lshft16_trunc_14_lowerout,
       lshft16_trunc_14_upperout, lshft16_trunc_15_lowerout, lshft16_trunc_15_upperout,
       lshft16_trunc_16_lowerout, lshft16_trunc_16_upperout, lshft16_trunc_17_lowerout,
       lshft16_trunc_17_upperout, lshft16_trunc_18_lowerout, lshft16_trunc_18_upperout,
       lshft16_trunc_19_lowerout, lshft16_trunc_19_upperout, lshft16_trunc_20_lowerout,
       lshft16_trunc_20_upperout, lshft16_trunc_21_lowerout, lshft16_trunc_21_upperout,
       lshft16_trunc_22_lowerout, lshft16_trunc_22_upperout, lshft16_trunc_23_lowerout,
       lshft16_trunc_23_upperout, lshft16_trunc_24_lowerout, lshft16_trunc_24_upperout,
       lshft16_trunc_25_lowerout, lshft16_trunc_25_upperout, lshft16_trunc_26_lowerout,
       lshft16_trunc_26_upperout, lshft16_trunc_27_lowerout, lshft16_trunc_27_upperout,
       lshft16_trunc_28_lowerout, lshft16_trunc_28_upperout, not_1_out;

  not not_1 (not_1_out[0], 1'b1);
  not not_2 (not_1_out[1], 1'b1);
  not not_3 (not_1_out[2], 1'b1);
  not not_4 (not_1_out[3], 1'b1);
  not not_5 (not_1_out[4], 1'b1);
  not not_6 (not_1_out[5], 1'b1);
  not not_7 (not_1_out[6], 1'b1);
  not not_8 (not_1_out[7], 1'b1);
  and8 and8_1 (.A(A), .B({8{B[0]}}), .O(and8_1_o));
  and8 and8_2 (.A(A), .B({8{B[1]}}), .O(and8_2_o));
  and8 and8_3 (.A(A), .B({8{B[2]}}), .O(and8_3_o));
  and8 and8_4 (.A(A), .B({8{B[3]}}), .O(and8_4_o));
  and8 and8_5 (.A(A), .B({8{B[4]}}), .O(and8_5_o));
  and8 and8_6 (.A(A), .B({8{B[5]}}), .O(and8_6_o));
  and8 and8_7 (.A(A), .B({8{B[6]}}), .O(and8_7_o));
  and8 and8_8 (.A(A), .B({8{B[7]}}), .O(and8_8_o));
  lshft16_trunc lshft16_trunc_1 (
    .lowerA(and8_2_o), .upperA(not_1_out), .lowerOut(lshft16_trunc_1_lowerout),
    .upperOut(lshft16_trunc_1_upperout));
  lshft16_trunc lshft16_trunc_2 (
    .lowerA(and8_3_o), .upperA(not_1_out), .lowerOut(lshft16_trunc_2_lowerout),
    .upperOut(lshft16_trunc_2_upperout));
  lshft16_trunc lshft16_trunc_3 (
    .lowerA(and8_4_o), .upperA(not_1_out), .lowerOut(lshft16_trunc_3_lowerout),
    .upperOut(lshft16_trunc_3_upperout));
  lshft16_trunc lshft16_trunc_4 (
    .lowerA(and8_5_o), .upperA(not_1_out), .lowerOut(lshft16_trunc_4_lowerout),
    .upperOut(lshft16_trunc_4_upperout));
  lshft16_trunc lshft16_trunc_5 (
    .lowerA(and8_6_o), .upperA(not_1_out), .lowerOut(lshft16_trunc_5_lowerout),
    .upperOut(lshft16_trunc_5_upperout));
  lshft16_trunc lshft16_trunc_6 (
    .lowerA(and8_7_o), .upperA(not_1_out), .lowerOut(lshft16_trunc_6_lowerout),
    .upperOut(lshft16_trunc_6_upperout));
  lshft16_trunc lshft16_trunc_7 (
    .lowerA(and8_8_o), .upperA(not_1_out), .lowerOut(lshft16_trunc_7_lowerout),
    .upperOut(lshft16_trunc_7_upperout));
  lshft16_trunc lshft16_trunc_8 (
    .lowerA(lshft16_trunc_2_lowerout), .upperA(lshft16_trunc_2_upperout),
    .lowerOut(lshft16_trunc_8_lowerout), .upperOut(lshft16_trunc_8_upperout));
  lshft16_trunc lshft16_trunc_9 (
    .lowerA(lshft16_trunc_3_lowerout), .upperA(lshft16_trunc_3_upperout),
    .lowerOut(lshft16_trunc_9_lowerout), .upperOut(lshft16_trunc_9_upperout));
  lshft16_trunc lshft16_trunc_10 (
    .lowerA(lshft16_trunc_4_lowerout), .upperA(lshft16_trunc_4_upperout),
    .lowerOut(lshft16_trunc_10_lowerout), .upperOut(lshft16_trunc_10_upperout));
  lshft16_trunc lshft16_trunc_11 (
    .lowerA(lshft16_trunc_5_lowerout), .upperA(lshft16_trunc_5_upperout),
    .lowerOut(lshft16_trunc_11_lowerout), .upperOut(lshft16_trunc_11_upperout));
  lshft16_trunc lshft16_trunc_12 (
    .lowerA(lshft16_trunc_6_lowerout), .upperA(lshft16_trunc_6_upperout),
    .lowerOut(lshft16_trunc_12_lowerout), .upperOut(lshft16_trunc_12_upperout));
  lshft16_trunc lshft16_trunc_13 (
    .lowerA(lshft16_trunc_7_lowerout), .upperA(lshft16_trunc_7_upperout),
    .lowerOut(lshft16_trunc_13_lowerout), .upperOut(lshft16_trunc_13_upperout));
  lshft16_trunc lshft16_trunc_14 (
    .lowerA(lshft16_trunc_9_lowerout), .upperA(lshft16_trunc_9_upperout),
    .lowerOut(lshft16_trunc_14_lowerout), .upperOut(lshft16_trunc_14_upperout));
  lshft16_trunc lshft16_trunc_15 (
    .lowerA(lshft16_trunc_10_lowerout), .upperA(lshft16_trunc_10_upperout),
    .lowerOut(lshft16_trunc_15_lowerout), .upperOut(lshft16_trunc_15_upperout));
  lshft16_trunc lshft16_trunc_16 (
    .lowerA(lshft16_trunc_11_lowerout), .upperA(lshft16_trunc_11_upperout),
    .lowerOut(lshft16_trunc_16_lowerout), .upperOut(lshft16_trunc_16_upperout));
  lshft16_trunc lshft16_trunc_17 (
    .lowerA(lshft16_trunc_12_lowerout), .upperA(lshft16_trunc_12_upperout),
    .lowerOut(lshft16_trunc_17_lowerout), .upperOut(lshft16_trunc_17_upperout));
  lshft16_trunc lshft16_trunc_18 (
    .lowerA(lshft16_trunc_13_lowerout), .upperA(lshft16_trunc_13_upperout),
    .lowerOut(lshft16_trunc_18_lowerout), .upperOut(lshft16_trunc_18_upperout));
  lshft16_trunc lshft16_trunc_19 (
    .lowerA(lshft16_trunc_15_lowerout), .upperA(lshft16_trunc_15_upperout),
    .lowerOut(lshft16_trunc_19_lowerout), .upperOut(lshft16_trunc_19_upperout));
  lshft16_trunc lshft16_trunc_20 (
    .lowerA(lshft16_trunc_16_lowerout), .upperA(lshft16_trunc_16_upperout),
    .lowerOut(lshft16_trunc_20_lowerout), .upperOut(lshft16_trunc_20_upperout));
  lshft16_trunc lshft16_trunc_21 (
    .lowerA(lshft16_trunc_17_lowerout), .upperA(lshft16_trunc_17_upperout),
    .lowerOut(lshft16_trunc_21_lowerout), .upperOut(lshft16_trunc_21_upperout));
  lshft16_trunc lshft16_trunc_22 (
    .lowerA(lshft16_trunc_18_lowerout), .upperA(lshft16_trunc_18_upperout),
    .lowerOut(lshft16_trunc_22_lowerout), .upperOut(lshft16_trunc_22_upperout));
  lshft16_trunc lshft16_trunc_23 (
    .lowerA(lshft16_trunc_20_lowerout), .upperA(lshft16_trunc_20_upperout),
    .lowerOut(lshft16_trunc_23_lowerout), .upperOut(lshft16_trunc_23_upperout));
  lshft16_trunc lshft16_trunc_24 (
    .lowerA(lshft16_trunc_21_lowerout), .upperA(lshft16_trunc_21_upperout),
    .lowerOut(lshft16_trunc_24_lowerout), .upperOut(lshft16_trunc_24_upperout));
  lshft16_trunc lshft16_trunc_25 (
    .lowerA(lshft16_trunc_22_lowerout), .upperA(lshft16_trunc_22_upperout),
    .lowerOut(lshft16_trunc_25_lowerout), .upperOut(lshft16_trunc_25_upperout));
  lshft16_trunc lshft16_trunc_26 (
    .lowerA(lshft16_trunc_24_lowerout), .upperA(lshft16_trunc_24_upperout),
    .lowerOut(lshft16_trunc_26_lowerout), .upperOut(lshft16_trunc_26_upperout));
  lshft16_trunc lshft16_trunc_27 (
    .lowerA(lshft16_trunc_25_lowerout), .upperA(lshft16_trunc_25_upperout),
    .lowerOut(lshft16_trunc_27_lowerout), .upperOut(lshft16_trunc_27_upperout));
  lshft16_trunc lshft16_trunc_28 (
    .lowerA(lshft16_trunc_27_lowerout), .upperA(lshft16_trunc_27_upperout),
    .lowerOut(lshft16_trunc_28_lowerout), .upperOut(lshft16_trunc_28_upperout));
  fullAdder16 fulladder16_1 (
    .lowerA(and8_1_o), .upperA(not_1_out), .lowerB(lshft16_trunc_1_lowerout),
    .UpperB(lshft16_trunc_1_upperout), .lowerSum(fulladder16_1_lowersum), .upperSum(fulladder16_1_uppersum),
    .CarryOut(fulladder16_1_carryout));  // open: CarryIn
  fullAdder16 fulladder16_2 (
    .lowerA(fulladder16_1_lowersum), .upperA(fulladder16_1_uppersum), .lowerB(lshft16_trunc_8_lowerout),
    .UpperB(lshft16_trunc_8_upperout), .CarryIn(fulladder16_1_carryout), .lowerSum(fulladder16_2_lowersum),
    .upperSum(fulladder16_2_uppersum), .CarryOut(fulladder16_2_carryout));
  fullAdder16 fulladder16_3 (
    .lowerA(fulladder16_2_lowersum), .upperA(fulladder16_2_uppersum), .lowerB(lshft16_trunc_14_lowerout),
    .UpperB(lshft16_trunc_14_upperout), .CarryIn(fulladder16_2_carryout), .lowerSum(fulladder16_3_lowersum),
    .upperSum(fulladder16_3_uppersum), .CarryOut(fulladder16_3_carryout));
  fullAdder16 fulladder16_4 (
    .lowerA(fulladder16_3_lowersum), .upperA(fulladder16_3_uppersum), .lowerB(lshft16_trunc_19_lowerout),
    .UpperB(lshft16_trunc_19_upperout), .CarryIn(fulladder16_3_carryout), .lowerSum(fulladder16_4_lowersum),
    .upperSum(fulladder16_4_uppersum), .CarryOut(fulladder16_4_carryout));
  fullAdder16 fulladder16_5 (
    .lowerA(fulladder16_4_lowersum), .upperA(fulladder16_4_uppersum), .lowerB(lshft16_trunc_23_lowerout),
    .UpperB(lshft16_trunc_23_upperout), .CarryIn(fulladder16_4_carryout), .lowerSum(fulladder16_5_lowersum),
    .upperSum(fulladder16_5_uppersum), .CarryOut(fulladder16_5_carryout));
  fullAdder16 fulladder16_6 (
    .lowerA(fulladder16_5_lowersum), .upperA(fulladder16_5_uppersum), .lowerB(lshft16_trunc_26_lowerout),
    .UpperB(lshft16_trunc_26_upperout), .CarryIn(fulladder16_5_carryout), .lowerSum(fulladder16_6_lowersum),
    .upperSum(fulladder16_6_uppersum), .CarryOut(fulladder16_6_carryout));
  fullAdder16 fulladder16_7 (
    .lowerA(fulladder16_6_lowersum), .upperA(fulladder16_6_uppersum), .lowerB(lshft16_trunc_28_lowerout),
    .UpperB(lshft16_trunc_28_upperout), .CarryIn(fulladder16_6_carryout), .lowerSum(lowerProduct),
    .upperSum(upperProduct));  // open: CarryOut
endmodule

module xor8 (
  input  [7:0] A,
  input  [7:0] B,
  output [7:0] O
);

  xor xor_1 (O[0], A[0], B[0]);
  xor xor_2 (O[1], A[1], B[1]);
  xor xor_3 (O[2], A[2], B[2]);
  xor xor_4 (O[3], A[3], B[3]);
  xor xor_5 (O[4], A[4], B[4]);
  xor xor_6 (O[5], A[5], B[5]);
  xor xor_7 (O[6], A[6], B[6]);
  xor xor_8 (O[7], A[7], B[7]);
endmodule

module and8 (
  input  [7:0] A,
  input  [7:0] B,
  output [7:0] O
);

  and and_1 (O[0], A[0], B[0]);
  and and_2 (O[1], A[1], B[1]);
  and and_3 (O[2], A[2], B[2]);
  and and_4 (O[3], A[3], B[3]);
  and and_5 (O[4], A[4], B[4]);
  and and_6 (O[5], A[5], B[5]);
  and and_7 (O[6], A[6], B[6]);
  and and_8 (O[7], A[7], B[7]);
endmodule

module or8 (
  input  [7:0] A,
  input  [7:0] B,
  output [7:0] O
);

  or or_1 (O[0], A[0], B[0]);
  or or_2 (O[1], A[1], B[1]);
  or or_3 (O[2], A[2], B[2]);
  or or_4 (O[3], A[3], B[3]);
  or or_5 (O[4], A[4], B[4]);
  or or_6 (O[5], A[5], B[5]);
  or or_7 (O[6], A[6], B[6]);
  or or_8 (O[7], A[7], B[7]);
endmodule

module buf8 (
  input  [7:0] A,
  output [7:0] O
);


  assign O = A;
endmodule

module integerDivide8 (
  input  [7:0] A,
  input  [7:0] B
);
endmodule

module lshft8 (
  input  [7:0] A,
  output [7:0] O
);


  assign O = {A[6:0], A[7]};
endmodule

module rshft8 (
  input  [7:0] A,
  output [7:0] O
);


  assign O = {A[0], A[7:1]};
endmodule

module lshft8_trunc (
  input  [7:0] A,
  output [7:0] O
);

  not not_1 (O[0], 1'b1);

  assign O[7:1] = A[6:0];
endmodule

module rshft8_trunc (
  input  [7:0] A,
  output [7:0] O
);

  not not_1 (O[7], 1'b1);

  assign O[6:0] = A[7:1];
endmodule

module fullAdder16 (
  input  [7:0] lowerA,
  input  [7:0] upperA,
  input  [7:0] lowerB,
  input  [7:0] UpperB,
  input  CarryIn,
  output [7:0] lowerSum,
  output [7:0] upperSum,
  output CarryOut
);

  wire halfadder_1_carryout, halfadder_2_carryout, halfadder_3_carryout, halfadder_4_carryout,
       halfadder_5_carryout, halfadder_6_carryout, halfadder_7_carryout, halfadder_8_carryout,
       halfadder_9_carryout, halfadder_10_carryout, halfadder_11_carryout, halfadder_12_carryout,
       halfadder_13_carryout, halfadder_14_carryout, halfadder_15_carryout;

  halfAdder halfadder_1 (
    .A(lowerA[0]), .B(lowerB[0]), .CarryIn(CarryIn), .Sum(lowerSum[0]), .CarryOut(halfadder_1_carryout));
  halfAdder halfadder_2 (
    .A(lowerA[1]), .B(lowerB[1]), .CarryIn(halfadder_1_carryout), .Sum(lowerSum[1]),
    .CarryOut(halfadder_2_carryout));
  halfAdder halfadder_3 (
    .A(lowerA[2]), .B(lowerB[2]), .CarryIn(halfadder_2_carryout), .Sum(lowerSum[2]),
    .CarryOut(halfadder_3_carryout));
  halfAdder halfadder_4 (
    .A(lowerA[3]), .B(lowerB[3]), .CarryIn(halfadder_3_carryout), .Sum(lowerSum[3]),
    .CarryOut(halfadder_4_carryout));
  halfAdder halfadder_5 (
    .A(lowerA[4]), .B(lowerB[4]), .CarryIn(halfadder_4_carryout), .Sum(lowerSum[4]),
    .CarryOut(halfadder_5_carryout));
  halfAdder halfadder_6 (
    .A(lowerA[5]), .B(lowerB[5]), .CarryIn(halfadder_5_carryout), .Sum(lowerSum[5]),
    .CarryOut(halfadder_6_carryout));
  halfAdder halfadder_7 (
    .A(lowerA[6]), .B(lowerB[6]), .CarryIn(halfadder_6_carryout), .Sum(lowerSum[6]),
    .CarryOut(halfadder_7_carryout));
  halfAdder halfadder_8 (
    .A(lowerA[7]), .B(lowerB[7]), .CarryIn(halfadder_7_carryout), .Sum(lowerSum[7]),
    .CarryOut(halfadder_8_carryout));
  halfAdder halfadder_9 (
    .A(upperA[0]), .B(UpperB[0]), .CarryIn(halfadder_8_carryout), .Sum(upperSum[0]),
    .CarryOut(halfadder_9_carryout));
  halfAdder halfadder_10 (
    .A(upperA[1]), .B(UpperB[1]), .CarryIn(halfadder_9_carryout), .Sum(upperSum[1]),
    .CarryOut(halfadder_10_carryout));
  halfAdder halfadder_11 (
    .A(upperA[2]), .B(UpperB[2]), .CarryIn(halfadder_10_carryout), .Sum(upperSum[2]),
    .CarryOut(halfadder_11_carryout));
  halfAdder halfadder_12 (
    .A(upperA[3]), .B(UpperB[3]), .CarryIn(halfadder_11_carryout), .Sum(upperSum[3]),
    .CarryOut(halfadder_12_carryout));
  halfAdder halfadder_13 (
    .A(upperA[4]), .B(UpperB[4]), .CarryIn(halfadder_12_carryout), .Sum(upperSum[4]),
    .CarryOut(halfadder_13_carryout));
  halfAdder halfadder_14 (
    .A(upperA[5]), .B(UpperB[5]), .CarryIn(halfadder_13_carryout), .Sum(upperSum[5]),
    .CarryOut(halfadder_14_carryout));
  halfAdder halfadder_15 (
    .A(upperA[6]), .B(UpperB[6]), .CarryIn(halfadder_14_carryout), .Sum(upperSum[6]),
    .CarryOut(halfadder_15_carryout));
  halfAdder halfadder_16 (
    .A(upperA[7]), .B(UpperB[7]), .CarryIn(halfadder_15_carryout), .Sum(upperSum[7]), .CarryOut(CarryOut));
endmodule

module lshft16_trunc (
  input  [7:0] lowerA,
  input  [7:0] upperA,
  output [7:0] lowerOut,
  output [7:0] upperOut
);

  not not_1 (lowerOut[0], 1'b1);

  assign lowerOut[7:1] = lowerA[6:0];
  assign upperOut = {upperA[6:0], lowerA[7]};
endmodule

module rshft16_trunc (
  input  [7:0] lowerA,
  input  [7:0] upperA,
  output [7:0] lowerOut,
  output [7:0] upperOut
);

  not not_1 (upperOut[7], 1'b1);

  assign lowerOut = {upperA[0], lowerA[7:1]};
  assign upperOut[6:0] = upperA[7:1];
endmodule
